// Logisim project life.circ as structural Verilog: 8 circuits, main circuit game
module MAKECELL (
  input  me,
  input  [7:0] neighbours,
  output result
);

  wire and_1_out, check2_3_1__2, check2_3_1__3;
  wire [3:0] bitadder_1_out;

  BitAdder bitadder_1 (.in0(neighbours), .out(bitadder_1_out));
  check2_3 check2_3_1 (.in_1(bitadder_1_out), ._2(check2_3_1__2), ._3(check2_3_1__3));
  and and_1 (and_1_out, me, check2_3_1__2);
  or or_1 (result, and_1_out, check2_3_1__3);
endmodule

module check2_3 (
  input  [3:0] in_1,
  output _2,
  output _3
);

  wire and_1_out, nor_1_out, not_1_out;

  and and_1 (and_1_out, in_1[1], nor_1_out);
  nor nor_1 (nor_1_out, in_1[2], in_1[3]);
  not not_1 (not_1_out, in_1[0]);
  and and_2 (_2, not_1_out, and_1_out);
  and and_3 (_3, in_1[0], and_1_out);
endmodule

module \cell  (
  input  N,
  input  S,
  input  E,
  input  W,
  input  NE,
  input  SE,
  input  SW,
  input  NW,
  input  clock,
  input  forse,
  input  reset,
  output me
);

  wire makecell_1_result;

  MAKECELL makecell_1 (.me(me), .neighbours({NW, SW, SE, NE, W, E, S, N}), .result(makecell_1_result));
  D_Flip_Flop d_ff_1 (.clk(clock), .D(makecell_1_result), .Q(me), .preset(forse), .reset(reset));  // open: Qn, en
endmodule

module row4 (
  input  [3:0] u,
  input  up,
  input  p,
  input  bp,
  input  un,
  input  n,
  input  bn,
  input  [3:0] set,
  input  reset,
  input  clock,
  input  [3:0] b,
  output [3:0] uo,
  output upo,
  output po,
  output bpo,
  output uno,
  output no,
  output bno,
  output [3:0] bo
);

  \cell  cell_1 (
    .N(u[0]), .S(b[0]), .E(bo[1]), .W(p), .NE(u[1]), .SE(b[1]), .SW(bp), .NW(up), .clock(clock),
    .forse(set[0]), .reset(reset), .me(bo[0]));
  \cell  cell_2 (
    .N(u[1]), .S(b[1]), .E(bo[2]), .W(bo[0]), .NE(u[2]), .SE(b[2]), .SW(b[0]), .NW(u[0]), .clock(clock),
    .forse(set[1]), .reset(reset), .me(bo[1]));
  \cell  cell_3 (
    .N(u[2]), .S(b[2]), .E(bo[3]), .W(bo[1]), .NE(u[3]), .SE(b[3]), .SW(b[1]), .NW(u[1]), .clock(clock),
    .forse(set[2]), .reset(reset), .me(bo[2]));
  \cell  cell_4 (
    .N(u[3]), .S(b[3]), .E(n), .W(bo[2]), .NE(un), .SE(bn), .SW(b[2]), .NW(u[2]), .clock(clock),
    .forse(set[3]), .reset(reset), .me(bo[3]));

  assign bno = b[3];
  assign bpo = b[0];
  assign no = bo[3];
  assign po = bo[0];
  assign uno = u[3];
  assign uo = bo;
  assign upo = u[0];

  // Other names for the same wires on the sheet: b1 = b[0]; b2 = b[1]; b3 = b[2]; b4 = b[3]; _1 = bo[0];
  //   out[3:0] = bo; _2 = bo[1]; _3 = bo[2]; _4 = bo[3]; set1 = set[0]; set2 = set[1]; set3 = set[2]; set4 = set[3];
  //   u1 = u[0]; u2 = u[1]; u3 = u[2]; u4 = u[3]
endmodule

module game (
);

  wire button_1_out, button_2_out, button_3_out, button_4_out, button_5_out, button_6_out, button_7_out,
       button_8_out, button_9_out, button_10_out, button_11_out, button_12_out, button_13_out, button_14_out,
       button_15_out, button_16_out, button_17_out, button_18_out, button_19_out, button_20_out,
       button_21_out, button_22_out, button_23_out, button_24_out, button_25_out, button_26_out,
       button_27_out, button_28_out, button_29_out, button_30_out, button_31_out, button_32_out,
       button_33_out, button_34_out, button_35_out, button_36_out, button_37_out, button_38_out,
       button_39_out, button_40_out, button_41_out, button_42_out, button_43_out, button_44_out,
       button_45_out, button_46_out, button_47_out, button_48_out, button_49_out, button_50_out,
       button_51_out, button_52_out, button_53_out, button_54_out, button_55_out, button_56_out,
       button_57_out, button_58_out, button_59_out, button_60_out, button_61_out, button_62_out,
       button_63_out, button_64_out, button_65_out, button_66_out, button_67_out, button_68_out,
       button_69_out, button_70_out, button_71_out, button_72_out, button_73_out, button_74_out,
       button_75_out, button_76_out, button_77_out, button_78_out, button_79_out, button_80_out,
       button_81_out, button_82_out, button_83_out, button_84_out, button_85_out, button_86_out,
       button_87_out, button_88_out, button_89_out, button_90_out, button_91_out, button_92_out,
       button_93_out, button_94_out, button_95_out, button_96_out, button_97_out, button_98_out,
       button_99_out, button_100_out, button_101_out, button_102_out, button_103_out, button_104_out,
       button_105_out, button_106_out, button_107_out, button_108_out, button_109_out, button_110_out,
       button_111_out, button_112_out, button_113_out, button_114_out, button_115_out, button_116_out,
       button_117_out, button_118_out, button_119_out, button_120_out, button_121_out, button_122_out,
       button_123_out, button_124_out, button_125_out, button_126_out, button_127_out, button_128_out,
       button_129_out, button_130_out, button_131_out, button_132_out, button_133_out, button_134_out,
       button_135_out, button_136_out, button_137_out, button_138_out, button_139_out, button_140_out,
       button_141_out, button_142_out, button_143_out, button_144_out, button_145_out, button_146_out,
       button_147_out, button_148_out, button_149_out, button_150_out, button_151_out, button_152_out,
       button_153_out, button_154_out, button_155_out, button_156_out, button_157_out, button_158_out,
       button_159_out, button_160_out, button_161_out, button_162_out, button_163_out, button_164_out,
       button_165_out, button_166_out, button_167_out, button_168_out, button_169_out, button_170_out,
       button_171_out, button_172_out, button_173_out, button_174_out, button_175_out, button_176_out,
       button_177_out, button_178_out, button_179_out, button_180_out, button_181_out, button_182_out,
       button_183_out, button_184_out, button_185_out, button_186_out, button_187_out, button_188_out,
       button_189_out, button_190_out, button_191_out, button_192_out, button_193_out, button_194_out,
       button_195_out, button_196_out, button_197_out, button_198_out, button_199_out, button_200_out,
       button_201_out, button_202_out, button_203_out, button_204_out, button_205_out, button_206_out,
       button_207_out, button_208_out, button_209_out, button_210_out, button_211_out, button_212_out,
       button_213_out, button_214_out, button_215_out, button_216_out, button_217_out, button_218_out,
       button_219_out, button_220_out, button_221_out, button_222_out, button_223_out, button_224_out,
       button_225_out, button_226_out, button_227_out, button_228_out, button_229_out, button_230_out,
       button_231_out, button_232_out, button_233_out, button_234_out, button_235_out, button_236_out,
       button_237_out, button_238_out, button_239_out, button_240_out, button_241_out, button_242_out,
       button_243_out, button_244_out, button_245_out, button_246_out, button_247_out, button_248_out,
       button_249_out, button_250_out, button_251_out, button_252_out, button_253_out, button_254_out,
       button_255_out, button_256_out, clock_1_out, reset_out;
  wire [15:0] buttonrow_1_set, buttonrow_2_set, buttonrow_3_set, buttonrow_4_set, buttonrow_5_set,
       buttonrow_6_set, buttonrow_7_set, buttonrow_8_set, buttonrow_9_set, buttonrow_10_set,
       buttonrow_11_set, buttonrow_12_set, buttonrow_13_set, buttonrow_14_set, buttonrow_15_set,
       buttonrow_16_set, storage_1_display1, storage_1_display2, storage_1_display3, storage_1_display4,
       storage_1_display5, storage_1_display6, storage_1_display7, storage_1_display8, storage_1_display9,
       storage_1_display10, storage_1_display11, storage_1_display12, storage_1_display13,
       storage_1_display14, storage_1_display15, storage_1_display16;

  Button button_1 (.out(button_1_out));
  Button button_2 (.out(button_2_out));
  Button button_3 (.out(button_3_out));
  Button button_4 (.out(button_4_out));
  Button button_5 (.out(button_5_out));
  Button button_6 (.out(button_6_out));
  Button button_7 (.out(button_7_out));
  Button button_8 (.out(button_8_out));
  Button button_9 (.out(button_9_out));
  Button button_10 (.out(button_10_out));
  Button button_11 (.out(button_11_out));
  Button button_12 (.out(button_12_out));
  Button button_13 (.out(button_13_out));
  Button button_14 (.out(button_14_out));
  Button button_15 (.out(button_15_out));
  Button button_16 (.out(button_16_out));
  Button button_17 (.out(button_17_out));
  Button button_18 (.out(button_18_out));
  Button button_19 (.out(button_19_out));
  Button button_20 (.out(button_20_out));
  Button button_21 (.out(button_21_out));
  Button button_22 (.out(button_22_out));
  Button button_23 (.out(button_23_out));
  Button button_24 (.out(button_24_out));
  Button button_25 (.out(button_25_out));
  Button button_26 (.out(button_26_out));
  Button button_27 (.out(button_27_out));
  Button button_28 (.out(button_28_out));
  Button button_29 (.out(button_29_out));
  Button button_30 (.out(button_30_out));
  Button button_31 (.out(button_31_out));
  Button button_32 (.out(button_32_out));
  Button button_33 (.out(button_33_out));
  Button button_34 (.out(button_34_out));
  Button button_35 (.out(button_35_out));
  Button button_36 (.out(button_36_out));
  Button button_37 (.out(button_37_out));
  Button button_38 (.out(button_38_out));
  Button button_39 (.out(button_39_out));
  Button button_40 (.out(button_40_out));
  Button button_41 (.out(button_41_out));
  Button button_42 (.out(button_42_out));
  Button button_43 (.out(button_43_out));
  Button button_44 (.out(button_44_out));
  Button button_45 (.out(button_45_out));
  Button button_46 (.out(button_46_out));
  Button button_47 (.out(button_47_out));
  Button button_48 (.out(button_48_out));
  Button button_49 (.out(button_49_out));
  Button button_50 (.out(button_50_out));
  Button button_51 (.out(button_51_out));
  Button button_52 (.out(button_52_out));
  Button button_53 (.out(button_53_out));
  Button button_54 (.out(button_54_out));
  Button button_55 (.out(button_55_out));
  Button button_56 (.out(button_56_out));
  Button button_57 (.out(button_57_out));
  Button button_58 (.out(button_58_out));
  Button button_59 (.out(button_59_out));
  Button button_60 (.out(button_60_out));
  Button button_61 (.out(button_61_out));
  Button button_62 (.out(button_62_out));
  Button button_63 (.out(button_63_out));
  Button button_64 (.out(button_64_out));
  Button button_65 (.out(button_65_out));
  Button button_66 (.out(button_66_out));
  Button button_67 (.out(button_67_out));
  Button button_68 (.out(button_68_out));
  Button button_69 (.out(button_69_out));
  Button button_70 (.out(button_70_out));
  Button button_71 (.out(button_71_out));
  Button button_72 (.out(button_72_out));
  Button button_73 (.out(button_73_out));
  Button button_74 (.out(button_74_out));
  Button button_75 (.out(button_75_out));
  Button button_76 (.out(button_76_out));
  Button button_77 (.out(button_77_out));
  Button button_78 (.out(button_78_out));
  Button button_79 (.out(button_79_out));
  Button button_80 (.out(button_80_out));
  Button button_81 (.out(button_81_out));
  Button button_82 (.out(button_82_out));
  Button button_83 (.out(button_83_out));
  Button button_84 (.out(button_84_out));
  Button button_85 (.out(button_85_out));
  Button button_86 (.out(button_86_out));
  Button button_87 (.out(button_87_out));
  Button button_88 (.out(button_88_out));
  Button button_89 (.out(button_89_out));
  Button button_90 (.out(button_90_out));
  Button button_91 (.out(button_91_out));
  Button button_92 (.out(button_92_out));
  Button button_93 (.out(button_93_out));
  Button button_94 (.out(button_94_out));
  Button button_95 (.out(button_95_out));
  Button button_96 (.out(button_96_out));
  Button button_97 (.out(button_97_out));
  Button button_98 (.out(button_98_out));
  Button button_99 (.out(button_99_out));
  Button button_100 (.out(button_100_out));
  Button button_101 (.out(button_101_out));
  Button button_102 (.out(button_102_out));
  Button button_103 (.out(button_103_out));
  Button button_104 (.out(button_104_out));
  Button button_105 (.out(button_105_out));
  Button button_106 (.out(button_106_out));
  Button button_107 (.out(button_107_out));
  Button button_108 (.out(button_108_out));
  Button button_109 (.out(button_109_out));
  Button button_110 (.out(button_110_out));
  Button button_111 (.out(button_111_out));
  Button button_112 (.out(button_112_out));
  Button button_113 (.out(button_113_out));
  Button button_114 (.out(button_114_out));
  Button button_115 (.out(button_115_out));
  Button button_116 (.out(button_116_out));
  buttonRow buttonrow_1 (
    ._1(button_1_out), ._2(button_3_out), ._3(button_2_out), ._4(button_51_out), ._5(button_52_out),
    ._6(button_49_out), ._7(button_50_out), ._8(button_114_out), ._9(button_113_out), ._10(button_115_out),
    ._11(button_116_out), ._12(button_179_out), ._13(button_178_out), ._14(button_180_out),
    ._15(button_177_out), ._16(button_241_out), .set(buttonrow_1_set));
  buttonRow buttonrow_2 (
    ._1(button_4_out), ._2(button_5_out), ._3(button_6_out), ._4(button_53_out), ._5(button_54_out),
    ._6(button_56_out), ._7(button_55_out), ._8(button_119_out), ._9(button_120_out), ._10(button_117_out),
    ._11(button_118_out), ._12(button_184_out), ._13(button_181_out), ._14(button_182_out),
    ._15(button_183_out), ._16(button_242_out), .set(buttonrow_2_set));
  Button button_117 (.out(button_117_out));
  Button button_118 (.out(button_118_out));
  Button button_119 (.out(button_119_out));
  Button button_120 (.out(button_120_out));
  Button button_121 (.out(button_121_out));
  buttonRow buttonrow_3 (
    ._1(button_7_out), ._2(button_8_out), ._3(button_9_out), ._4(button_57_out), ._5(button_60_out),
    ._6(button_59_out), ._7(button_58_out), ._8(button_123_out), ._9(button_124_out), ._10(button_122_out),
    ._11(button_121_out), ._12(button_187_out), ._13(button_186_out), ._14(button_188_out),
    ._15(button_185_out), ._16(button_243_out), .set(buttonrow_3_set));
  Button button_122 (.out(button_122_out));
  Button button_123 (.out(button_123_out));
  Button button_124 (.out(button_124_out));
  Button button_125 (.out(button_125_out));
  Button button_126 (.out(button_126_out));
  Button button_127 (.out(button_127_out));
  buttonRow buttonrow_4 (
    ._1(button_12_out), ._2(button_11_out), ._3(button_10_out), ._4(button_61_out), ._5(button_63_out),
    ._6(button_62_out), ._7(button_64_out), ._8(button_125_out), ._9(button_128_out), ._10(button_126_out),
    ._11(button_127_out), ._12(button_191_out), ._13(button_192_out), ._14(button_189_out),
    ._15(button_190_out), ._16(button_244_out), .set(buttonrow_4_set));
  Button button_128 (.out(button_128_out));
  Button button_129 (.out(button_129_out));
  Button button_130 (.out(button_130_out));
  buttonRow buttonrow_5 (
    ._1(button_14_out), ._2(button_13_out), ._3(button_15_out), ._4(button_67_out), ._5(button_66_out),
    ._6(button_65_out), ._7(button_68_out), ._8(button_131_out), ._9(button_129_out), ._10(button_130_out),
    ._11(button_132_out), ._12(button_195_out), ._13(button_193_out), ._14(button_194_out),
    ._15(button_196_out), ._16(button_245_out), .set(buttonrow_5_set));
  Button button_131 (.out(button_131_out));
  Button button_132 (.out(button_132_out));
  Button button_133 (.out(button_133_out));
  Button button_134 (.out(button_134_out));
  Button button_135 (.out(button_135_out));
  Button button_136 (.out(button_136_out));
  buttonRow buttonrow_6 (
    ._1(button_16_out), ._2(button_18_out), ._3(button_17_out), ._4(button_71_out), ._5(button_69_out),
    ._6(button_70_out), ._7(button_72_out), ._8(button_136_out), ._9(button_135_out), ._10(button_134_out),
    ._11(button_133_out), ._12(button_198_out), ._13(button_199_out), ._14(button_200_out),
    ._15(button_197_out), ._16(button_246_out), .set(buttonrow_6_set));
  Button button_137 (.out(button_137_out));
  Button button_138 (.out(button_138_out));
  Button button_139 (.out(button_139_out));
  buttonRow buttonrow_7 (
    ._1(button_21_out), ._2(button_20_out), ._3(button_19_out), ._4(button_74_out), ._5(button_73_out),
    ._6(button_75_out), ._7(button_76_out), ._8(button_140_out), ._9(button_139_out), ._10(button_137_out),
    ._11(button_138_out), ._12(button_201_out), ._13(button_204_out), ._14(button_202_out),
    ._15(button_203_out), ._16(button_247_out), .set(buttonrow_7_set));
  Button button_140 (.out(button_140_out));
  Button button_141 (.out(button_141_out));
  Button button_142 (.out(button_142_out));
  Button button_143 (.out(button_143_out));
  buttonRow buttonrow_8 (
    ._1(button_22_out), ._2(button_23_out), ._3(button_24_out), ._4(button_80_out), ._5(button_78_out),
    ._6(button_79_out), ._7(button_77_out), ._8(button_141_out), ._9(button_143_out), ._10(button_144_out),
    ._11(button_142_out), ._12(button_205_out), ._13(button_208_out), ._14(button_207_out),
    ._15(button_206_out), ._16(button_248_out), .set(buttonrow_8_set));
  Button button_144 (.out(button_144_out));
  Button button_145 (.out(button_145_out));
  Button button_146 (.out(button_146_out));
  Button button_147 (.out(button_147_out));
  buttonRow buttonrow_9 (
    ._1(button_25_out), ._2(button_27_out), ._3(button_26_out), ._4(button_83_out), ._5(button_84_out),
    ._6(button_81_out), ._7(button_82_out), ._8(button_145_out), ._9(button_147_out), ._10(button_146_out),
    ._11(button_148_out), ._12(button_212_out), ._13(button_209_out), ._14(button_211_out),
    ._15(button_210_out), ._16(button_249_out), .set(buttonrow_9_set));
  Button button_148 (.out(button_148_out));
  buttonRow buttonrow_10 (
    ._1(button_30_out), ._2(button_28_out), ._3(button_29_out), ._4(button_87_out), ._5(button_88_out),
    ._6(button_85_out), ._7(button_86_out), ._8(button_150_out), ._9(button_152_out), ._10(button_149_out),
    ._11(button_151_out), ._12(button_215_out), ._13(button_216_out), ._14(button_214_out),
    ._15(button_213_out), ._16(button_250_out), .set(buttonrow_10_set));
  Button button_149 (.out(button_149_out));
  Button button_150 (.out(button_150_out));
  Button button_151 (.out(button_151_out));
  Button button_152 (.out(button_152_out));
  Button button_153 (.out(button_153_out));
  buttonRow buttonrow_11 (
    ._1(button_31_out), ._2(button_33_out), ._3(button_32_out), ._4(button_92_out), ._5(button_91_out),
    ._6(button_90_out), ._7(button_89_out), ._8(button_154_out), ._9(button_153_out), ._10(button_156_out),
    ._11(button_155_out), ._12(button_220_out), ._13(button_219_out), ._14(button_218_out),
    ._15(button_217_out), ._16(button_251_out), .set(buttonrow_11_set));
  Button button_154 (.out(button_154_out));
  Button button_155 (.out(button_155_out));
  Button button_156 (.out(button_156_out));
  buttonRow buttonrow_12 (
    ._1(button_36_out), ._2(button_35_out), ._3(button_34_out), ._4(button_94_out), ._5(button_93_out),
    ._6(button_96_out), ._7(button_95_out), ._8(button_157_out), ._9(button_160_out), ._10(button_159_out),
    ._11(button_158_out), ._12(button_222_out), ._13(button_224_out), ._14(button_221_out),
    ._15(button_223_out), ._16(button_252_out), .set(buttonrow_12_set));
  Button button_157 (.out(button_157_out));
  Button button_158 (.out(button_158_out));
  Button button_159 (.out(button_159_out));
  Button button_160 (.out(button_160_out));
  Button button_161 (.out(button_161_out));
  Button button_162 (.out(button_162_out));
  buttonRow buttonrow_13 (
    ._1(button_37_out), ._2(button_39_out), ._3(button_38_out), ._4(button_98_out), ._5(button_97_out),
    ._6(button_100_out), ._7(button_99_out), ._8(button_164_out), ._9(button_162_out), ._10(button_163_out),
    ._11(button_161_out), ._12(button_227_out), ._13(button_228_out), ._14(button_225_out),
    ._15(button_226_out), ._16(button_253_out), .set(buttonrow_13_set));
  Button button_163 (.out(button_163_out));
  Button button_164 (.out(button_164_out));
  Button button_165 (.out(button_165_out));
  Button button_166 (.out(button_166_out));
  Button button_167 (.out(button_167_out));
  Button button_168 (.out(button_168_out));
  buttonRow buttonrow_14 (
    ._1(button_42_out), ._2(button_40_out), ._3(button_41_out), ._4(button_103_out), ._5(button_102_out),
    ._6(button_104_out), ._7(button_101_out), ._8(button_166_out), ._9(button_168_out), ._10(button_167_out),
    ._11(button_165_out), ._12(button_229_out), ._13(button_231_out), ._14(button_232_out),
    ._15(button_230_out), ._16(button_254_out), .set(buttonrow_14_set));
  Button button_169 (.out(button_169_out));
  Button button_170 (.out(button_170_out));
  buttonRow buttonrow_15 (
    ._1(button_43_out), ._2(button_45_out), ._3(button_44_out), ._4(button_107_out), ._5(button_108_out),
    ._6(button_105_out), ._7(button_106_out), ._8(button_169_out), ._9(button_172_out), ._10(button_171_out),
    ._11(button_170_out), ._12(button_236_out), ._13(button_235_out), ._14(button_234_out),
    ._15(button_233_out), ._16(button_255_out), .set(buttonrow_15_set));
  Button button_171 (.out(button_171_out));
  Button button_172 (.out(button_172_out));
  Button button_173 (.out(button_173_out));
  Button button_174 (.out(button_174_out));
  buttonRow buttonrow_16 (
    ._1(button_46_out), ._2(button_47_out), ._3(button_48_out), ._4(button_111_out), ._5(button_110_out),
    ._6(button_109_out), ._7(button_112_out), ._8(button_176_out), ._9(button_173_out), ._10(button_175_out),
    ._11(button_174_out), ._12(button_238_out), ._13(button_237_out), ._14(button_239_out),
    ._15(button_240_out), ._16(button_256_out), .set(buttonrow_16_set));
  Button button_175 (.out(button_175_out));
  Button button_176 (.out(button_176_out));
  Clock clock_1 (.out(clock_1_out));
  Button reset (.out(reset_out));
  Button button_177 (.out(button_177_out));
  Button button_178 (.out(button_178_out));
  Button button_179 (.out(button_179_out));
  Button button_180 (.out(button_180_out));
  Button button_181 (.out(button_181_out));
  Button button_182 (.out(button_182_out));
  Button button_183 (.out(button_183_out));
  Button button_184 (.out(button_184_out));
  Button button_185 (.out(button_185_out));
  Button button_186 (.out(button_186_out));
  Button button_187 (.out(button_187_out));
  Button button_188 (.out(button_188_out));
  Button button_189 (.out(button_189_out));
  Button button_190 (.out(button_190_out));
  Button button_191 (.out(button_191_out));
  Button button_192 (.out(button_192_out));
  Button button_193 (.out(button_193_out));
  Button button_194 (.out(button_194_out));
  Button button_195 (.out(button_195_out));
  Button button_196 (.out(button_196_out));
  Button button_197 (.out(button_197_out));
  Button button_198 (.out(button_198_out));
  Button button_199 (.out(button_199_out));
  Button button_200 (.out(button_200_out));
  Button button_201 (.out(button_201_out));
  Button button_202 (.out(button_202_out));
  Button button_203 (.out(button_203_out));
  Button button_204 (.out(button_204_out));
  Button button_205 (.out(button_205_out));
  Button button_206 (.out(button_206_out));
  Button button_207 (.out(button_207_out));
  Button button_208 (.out(button_208_out));
  Button button_209 (.out(button_209_out));
  Button button_210 (.out(button_210_out));
  Button button_211 (.out(button_211_out));
  Button button_212 (.out(button_212_out));
  Button button_213 (.out(button_213_out));
  Button button_214 (.out(button_214_out));
  Button button_215 (.out(button_215_out));
  Button button_216 (.out(button_216_out));
  Button button_217 (.out(button_217_out));
  Button button_218 (.out(button_218_out));
  Button button_219 (.out(button_219_out));
  Button button_220 (.out(button_220_out));
  Button button_221 (.out(button_221_out));
  Button button_222 (.out(button_222_out));
  Button button_223 (.out(button_223_out));
  Button button_224 (.out(button_224_out));
  Button button_225 (.out(button_225_out));
  Button button_226 (.out(button_226_out));
  Button button_227 (.out(button_227_out));
  Button button_228 (.out(button_228_out));
  Button button_229 (.out(button_229_out));
  Button button_230 (.out(button_230_out));
  Button button_231 (.out(button_231_out));
  Button button_232 (.out(button_232_out));
  Button button_233 (.out(button_233_out));
  Button button_234 (.out(button_234_out));
  Button button_235 (.out(button_235_out));
  Button button_236 (.out(button_236_out));
  Button button_237 (.out(button_237_out));
  Button button_238 (.out(button_238_out));
  Button button_239 (.out(button_239_out));
  Button button_240 (.out(button_240_out));
  Button button_241 (.out(button_241_out));
  Button button_242 (.out(button_242_out));
  Button button_243 (.out(button_243_out));
  Button button_244 (.out(button_244_out));
  Button button_245 (.out(button_245_out));
  Button button_246 (.out(button_246_out));
  Button button_247 (.out(button_247_out));
  Button button_248 (.out(button_248_out));
  Button button_249 (.out(button_249_out));
  Button button_250 (.out(button_250_out));
  Button button_251 (.out(button_251_out));
  Button button_252 (.out(button_252_out));
  Button button_253 (.out(button_253_out));
  Button button_254 (.out(button_254_out));
  Button button_255 (.out(button_255_out));
  Button button_256 (.out(button_256_out));
  DotMatrix #(.inputtype("row"), .matrixcols(16), .matrixrows(16), .dotshape("circle")) dotmatrix_1 (
    .row0(storage_1_display1), .row1(storage_1_display2), .row2(storage_1_display3),
    .row3(storage_1_display4), .row4(storage_1_display5), .row5(storage_1_display6),
    .row6(storage_1_display7), .row7(storage_1_display8), .row8(storage_1_display9),
    .row9(storage_1_display10), .row10(storage_1_display11), .row11(storage_1_display12),
    .row12(storage_1_display13), .row13(storage_1_display14), .row14(storage_1_display15),
    .row15(storage_1_display16));
  storage storage_1 (
    .clock(clock_1_out), .set1(buttonrow_1_set), .set2(buttonrow_2_set), .set3(buttonrow_3_set),
    .set4(buttonrow_4_set), .set5(buttonrow_5_set), .set6(buttonrow_6_set), .set7(buttonrow_7_set),
    .set8(buttonrow_8_set), .display1(storage_1_display1), .display2(storage_1_display2),
    .display3(storage_1_display3), .display4(storage_1_display4), .display5(storage_1_display5),
    .display6(storage_1_display6), .display7(storage_1_display7), .display8(storage_1_display8),
    .reset(reset_out), .set9(buttonrow_9_set), .display9(storage_1_display9), .set10(buttonrow_10_set),
    .display10(storage_1_display10), .set11(buttonrow_11_set), .display11(storage_1_display11),
    .set12(buttonrow_12_set), .display12(storage_1_display12), .set13(buttonrow_13_set),
    .display13(storage_1_display13), .set14(buttonrow_14_set), .display14(storage_1_display14),
    .set15(buttonrow_15_set), .display15(storage_1_display15), .set16(buttonrow_16_set),
    .display16(storage_1_display16));
endmodule

module row (
  input  clock,
  input  [15:0] set,
  input  [15:0] up,
  input  [15:0] down,
  input  reset,
  output [15:0] displayOut,
  output [15:0] upOut,
  output [15:0] downOut
);

  wire row4_1_bno, row4_1_bpo, row4_1_no, row4_1_po, row4_1_uno, row4_1_upo, row4_2_bno, row4_2_bpo,
       row4_2_no, row4_2_po, row4_2_uno, row4_2_upo, row4_3_bno, row4_3_bpo, row4_3_no, row4_3_po,
       row4_3_uno, row4_3_upo, row4_4_bno, row4_4_bpo, row4_4_no, row4_4_po, row4_4_uno, row4_4_upo;

  row4 row4_1 (
    .up(row4_4_uno), .p(row4_4_no), .bp(row4_4_bno), .un(row4_2_upo), .upo(row4_1_upo), .n(row4_2_po),
    .po(row4_1_po), .bn(row4_2_bpo), .bpo(row4_1_bpo), .uno(row4_1_uno), .no(row4_1_no), .set(set[3:0]),
    .bno(row4_1_bno), .reset(reset), .clock(clock), .u(up[3:0]),
    .uo({displayOut[12], displayOut[13], displayOut[14], displayOut[15]}), .b(down[3:0]), .bo(downOut[3:0]));
  row4 row4_2 (
    .up(row4_1_uno), .p(row4_1_no), .bp(row4_1_bno), .un(row4_3_upo), .upo(row4_2_upo), .n(row4_3_po),
    .po(row4_2_po), .bn(row4_3_bpo), .bpo(row4_2_bpo), .uno(row4_2_uno), .no(row4_2_no), .set(set[7:4]),
    .bno(row4_2_bno), .reset(reset), .clock(clock), .u(up[7:4]),
    .uo({displayOut[8], displayOut[9], displayOut[10], displayOut[11]}), .b(down[7:4]), .bo(downOut[7:4]));
  row4 row4_3 (
    .up(row4_2_uno), .p(row4_2_no), .bp(row4_2_bno), .un(row4_4_upo), .upo(row4_3_upo), .n(row4_4_po),
    .po(row4_3_po), .bn(row4_4_bpo), .bpo(row4_3_bpo), .uno(row4_3_uno), .no(row4_3_no), .set(set[11:8]),
    .bno(row4_3_bno), .reset(reset), .clock(clock), .u(up[11:8]),
    .uo({displayOut[4], displayOut[5], displayOut[6], displayOut[7]}), .b(down[11:8]), .bo(downOut[11:8]));
  row4 row4_4 (
    .up(row4_3_uno), .p(row4_3_no), .bp(row4_3_bno), .un(row4_1_upo), .upo(row4_4_upo), .n(row4_1_po),
    .po(row4_4_po), .bn(row4_1_bpo), .bpo(row4_4_bpo), .uno(row4_4_uno), .no(row4_4_no), .set(set[15:12]),
    .bno(row4_4_bno), .reset(reset), .clock(clock), .u(up[15:12]),
    .uo({displayOut[0], displayOut[1], displayOut[2], displayOut[3]}), .b(down[15:12]), .bo(downOut[15:12]));

  assign upOut = {displayOut[0], displayOut[1], displayOut[2], displayOut[3], displayOut[4], displayOut[5], displayOut[6], displayOut[7], displayOut[8], displayOut[9], displayOut[10], displayOut[11], displayOut[12], displayOut[13], displayOut[14], displayOut[15]};

  // Other names for the same wires on the sheet: d3[3:0] = down[11:8]; d4[3:0] = down[15:12];
  //   do3[3:0] = downOut[11:8]; do4[3:0] = downOut[15:12]; d1[3:0] = down[3:0]; d2[3:0] = down[7:4];
  //   do1[3:0] = downOut[3:0]; do2[3:0] = downOut[7:4]; set1[3:0] = set[3:0]; set2[3:0] = set[7:4];
  //   set3[3:0] = set[11:8]; set4[3:0] = set[15:12]; u3[3:0] = up[11:8]; u4[3:0] = up[15:12];
  //   uo3[3:0] = {displayOut[4], displayOut[5], displayOut[6], displayOut[7]};
  //   uo4[3:0] = {displayOut[0], displayOut[1], displayOut[2], displayOut[3]}; u1[3:0] = up[3:0]; u2[3:0] = up[7:4];
  //   uo1[3:0] = {displayOut[12], displayOut[13], displayOut[14], displayOut[15]};
  //   uo2[3:0] = {displayOut[8], displayOut[9], displayOut[10], displayOut[11]}
endmodule

module storage (
  input  clock,
  input  reset,
  input  [15:0] set1,
  input  [15:0] set2,
  input  [15:0] set3,
  input  [15:0] set4,
  input  [15:0] set5,
  input  [15:0] set6,
  input  [15:0] set7,
  input  [15:0] set8,
  input  [15:0] set9,
  input  [15:0] set10,
  input  [15:0] set11,
  input  [15:0] set12,
  input  [15:0] set13,
  input  [15:0] set14,
  input  [15:0] set15,
  input  [15:0] set16,
  output [15:0] display1,
  output [15:0] display2,
  output [15:0] display3,
  output [15:0] display4,
  output [15:0] display5,
  output [15:0] display6,
  output [15:0] display7,
  output [15:0] display8,
  output [15:0] display9,
  output [15:0] display10,
  output [15:0] display11,
  output [15:0] display12,
  output [15:0] display13,
  output [15:0] display14,
  output [15:0] display15,
  output [15:0] display16
);

  wire [15:0] row_1_downout, row_1_upout, row_2_downout, row_2_upout, row_3_downout, row_3_upout,
       row_4_downout, row_4_upout, row_5_downout, row_5_upout, row_6_downout, row_6_upout, row_7_downout,
       row_7_upout, row_8_downout, row_8_upout, row_9_downout, row_9_upout, row_10_downout, row_10_upout,
       row_11_downout, row_11_upout, row_12_downout, row_12_upout, row_13_downout, row_13_upout,
       row_14_downout, row_14_upout, row_15_downout, row_15_upout, row_16_downout, row_16_upout;

  row row_1 (
    .clock(clock), .set(set1), .up(row_16_downout), .down(row_2_upout), .upOut(row_1_upout),
    .downOut(row_1_downout), .reset(reset), .displayOut(display1));
  row row_2 (
    .clock(clock), .set(set2), .up(row_1_downout), .down(row_3_upout), .upOut(row_2_upout),
    .downOut(row_2_downout), .reset(reset), .displayOut(display2));
  row row_3 (
    .clock(clock), .set(set3), .up(row_2_downout), .down(row_4_upout), .upOut(row_3_upout),
    .downOut(row_3_downout), .reset(reset), .displayOut(display3));
  row row_4 (
    .clock(clock), .set(set4), .up(row_3_downout), .down(row_5_upout), .upOut(row_4_upout),
    .downOut(row_4_downout), .reset(reset), .displayOut(display4));
  row row_5 (
    .clock(clock), .set(set5), .up(row_4_downout), .down(row_6_upout), .upOut(row_5_upout),
    .downOut(row_5_downout), .reset(reset), .displayOut(display5));
  row row_6 (
    .clock(clock), .set(set6), .up(row_5_downout), .down(row_7_upout), .upOut(row_6_upout),
    .downOut(row_6_downout), .reset(reset), .displayOut(display6));
  row row_7 (
    .clock(clock), .set(set7), .up(row_6_downout), .down(row_8_upout), .upOut(row_7_upout),
    .downOut(row_7_downout), .reset(reset), .displayOut(display7));
  row row_8 (
    .clock(clock), .set(set8), .up(row_7_downout), .down(row_9_upout), .upOut(row_8_upout),
    .downOut(row_8_downout), .reset(reset), .displayOut(display8));
  row row_9 (
    .clock(clock), .set(set9), .up(row_8_downout), .down(row_10_upout), .upOut(row_9_upout),
    .downOut(row_9_downout), .reset(reset), .displayOut(display9));
  row row_10 (
    .clock(clock), .set(set10), .up(row_9_downout), .down(row_11_upout), .upOut(row_10_upout),
    .downOut(row_10_downout), .reset(reset), .displayOut(display10));
  row row_11 (
    .clock(clock), .set(set11), .up(row_10_downout), .down(row_12_upout), .upOut(row_11_upout),
    .downOut(row_11_downout), .reset(reset), .displayOut(display11));
  row row_12 (
    .clock(clock), .set(set12), .up(row_11_downout), .down(row_13_upout), .upOut(row_12_upout),
    .downOut(row_12_downout), .reset(reset), .displayOut(display12));
  row row_13 (
    .clock(clock), .set(set13), .up(row_12_downout), .down(row_14_upout), .upOut(row_13_upout),
    .downOut(row_13_downout), .reset(reset), .displayOut(display13));
  row row_14 (
    .clock(clock), .set(set14), .up(row_13_downout), .down(row_15_upout), .upOut(row_14_upout),
    .downOut(row_14_downout), .reset(reset), .displayOut(display14));
  row row_15 (
    .clock(clock), .set(set15), .up(row_14_downout), .down(row_16_upout), .upOut(row_15_upout),
    .downOut(row_15_downout), .reset(reset), .displayOut(display15));
  row row_16 (
    .clock(clock), .set(set16), .up(row_15_downout), .down(row_1_upout), .upOut(row_16_upout),
    .downOut(row_16_downout), .reset(reset), .displayOut(display16));
endmodule

module buttonRow (
  input  _1,
  input  _2,
  input  _3,
  input  _4,
  input  _5,
  input  _6,
  input  _7,
  input  _8,
  input  _9,
  input  _10,
  input  _11,
  input  _12,
  input  _13,
  input  _14,
  input  _15,
  input  _16,
  output [15:0] set
);


  assign set = {_16, _15, _14, _13, _12, _11, _10, _9, _8, _7, _6, _5, _4, _3, _2, _1};
endmodule
